# Fritzing sketch strip_controller_board_rev2 (saved by Fritzing 0.9.3b)
circuit board: 5.41743cm x 4.72073cm
breadboards: 1

parts:
  Q1 = NPN-Transistor [package="TO92 [THT]"]
  Q4 = npn-Powertransistor [package="TO220 [THT]"]
  R1 = Resistor [tolerance=±5% resistance=1k package=THT]
  R3 = Resistor [tolerance=±5% resistance=1k package=THT]
  R2 = Resistor [tolerance=±5% resistance=1k package=THT]
  R4 = Resistor [tolerance=±5% resistance=10k package=THT]
  Q2 = NPN-Transistor [package="TO92 [THT]"]
  Q3 = NPN-Transistor [package="TO92 [THT]"]
  Q6 = npn-Powertransistor [package="TO220 [THT]"]
  Q5 = npn-Powertransistor [package="TO220 [THT]"]
  R5 = Resistor [tolerance=±5% resistance=10k package=THT]
  R6 = Resistor [tolerance=±5% resistance=10k package=THT]
  J2 = female pin header, 4 pins [form="♀ (female)"]
  IC1 = IC, DIP package, 14 pins [chip_label=IC]
  U1 = RJ45 Jack [package=rj45-8]
  U2 = RJ45 Jack [package=rj45-8]

nets:
  N1: Q1.E, Q4.emitter, Q2.E, Q3.E, Q6.emitter, Q5.emitter, IC1.pin1, U1.1, U1.3, U1.5, U2.1, U2.3, U2.5
  N2: Q1.B, R1.Pin_1
  N3: Q1.C, Q4.base, R4.Pin_0
  N4: Q4.collector, J2.pin4
  N5: R1.Pin_0, IC1.pin10
  N6: R3.Pin_0, IC1.pin7
  N7: R3.Pin_1, Q3.B
  N8: R2.Pin_0, IC1.pin9
  N9: R2.Pin_1, Q2.B
  N10: R4.Pin_1, R5.Pin_1, R6.Pin_1, J2.pin1, U1.7, U1.8, U2.7, U2.8
  N11: Q2.C, Q5.base, R5.Pin_0
  N12: Q3.C, Q6.base, R6.Pin_0
  N13: Q6.collector, J2.pin2
  N14: Q5.collector, J2.pin3
  N15: IC1.pin6, U1.2, U2.2
  N16: IC1.pin8, U1.4, U2.4
  N17: IC1.pin11, IC1.pin14, U1.6, U2.6

notes:
  GND
  SCL
  SDA
  VCC
  +
  R
  G
  B
  LEDstrip Controller v1.0
  12V
